# Fritzing sketch testBoard (saved by Fritzing 0.9.3b)
breadboards: 1

parts:
  U1 = PCF8575C [package=so-24dw]
  Part1 = Arduino Uno (Rev3)
  S1 = Pushbutton [package="[THT]"]
  R1 = Resistor [tolerance=±5% resistance=10k package=THT]
  LED1 = LED - 5mm [color="Red (633nm)" package="5 mm [THT]"]
  R2 = Resistor [tolerance=±5% resistance=220 package=THT]

nets:
  N1: U1.INT, Part1.D2
  VCC: U1.PO0, U1.VCC, Part1.5V, S1.Pin_3, S1.Pin_4
  N2: U1.PO1, LED1.anode
  GND: U1.GND, Part1.GND, R1.Pin_0, R2.Pin_1
  N3: U1.SCL, Part1.A5/SCL
  N4: U1.SDA, Part1.A4/SDA
  N5: S1.Pin_1, S1.Pin_2, R1.Pin_1
  N6: LED1.cathode, R2.Pin_0

notes:
  SDA
  SCL
  INT
  P0
  P1
